# Fritzing sketch a3_RGBLed (saved by Fritzing 0.9.3b)
breadboards: 1

parts:
  LED3 = RGB LED (com. cathode, rbg) [package="5 mm [THT]"]
  元件1 = Adafruit T-Cobbler Plus [part_number="Adafruit #1989 and #2028"]
  R1 = Resistor [tolerance=±5% resistance=220 package=THT]
  R2 = Resistor [tolerance=±5% resistance=220 package=THT]
  R3 = Resistor [tolerance=±5% resistance=220 package=THT]

nets:
  N1: LED3.red_anode, R1.Pin_1
  N2: LED3.blue_anode, R2.Pin_1
  N3: LED3.green_anode, R3.Pin_1
  N4: 元件1.GPIO17, R3.Pin_0
  N5: 元件1.GPIO27, R2.Pin_0
  N6: 元件1.GPIO22, R1.Pin_0

custom parts:
  Adafruit T-Cobbler Plus: The Raspberry Pi has landed on the Maker World like a 40-GPIO pinned, quad-USB ported, credit card sized bomb of DIY joy. And while you can use most of our great Model B accessories by hooking up our downgrade cable, its probably a good time to upgrade your set up and accessorize using all of the 40 pins. That's why we now carry the Assembled Adafruit Pi T-Cobbler Plus - Breakout + Cable for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
