# Fritzing sketch mcp3008 (saved by Fritzing 0.9.2b)
breadboards: 1

parts:
  元件1 = Adafruit T-Cobbler Plus [part_number="Adafruit #1989 and #2028"]
  IC1 = MCP3008 8-channel 10-bit ADC [part_number=MCP3008]  # not connected
  R1 = PHOTOCELL [package=photocell-kit]
  R2 = Resistor [tolerance=±5% resistance=220 package=THT]
  T1 = LM35 Temperature Sensor [package="TO92 [THT]"]

nets:
  N1: 元件1.+3.3V, R1.P$1, T1.+Vs
  GND: 元件1.GND, R2.Pin_0, T1.GND
  N2: R1.P$2, R2.Pin_1

custom parts:
  Adafruit T-Cobbler Plus: The Raspberry Pi has landed on the Maker World like a 40-GPIO pinned, quad-USB ported, credit card sized bomb of DIY joy. And while you can use most of our great Model B accessories by hooking up our downgrade cable, its probably a good time to upgrade your set up and accessorize using all of the 40 pins. That's why we now carry the Assembled Adafruit Pi T-Cobbler Plus - Breakout + Cable for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
