# Fritzing sketch rfid (saved by Fritzing 0.9.3b)
breadboards: 1

parts:
  Part3 = RFID-RC522-v2
  元件2 = Adafruit T-Cobbler Plus [part_number="Adafruit #1989 and #2028"]
  LCD2 = LCD screen
  LCM1602_IIC3 = LCM1602 IIC [part_number="LCM1602 IIC" chip_label="LCM1602 IIC" package="DIP (Dual Inline) [THT]"]
  J1 = Piezo Speaker

nets:
  N1: Part3.SCK, 元件2.GPIO25
  N2: Part3.MOSI, 元件2.CE0
  N3: Part3.MISO, 元件2.MOSI
  N4: Part3.IRQ, 元件2.MISO
  N5: Part3.GND, 元件2.SCLK
  N6: Part3.3_3V, 元件2.+3.3V
  N7: 元件2.SDA, LCM1602_IIC3.SDA
  N8: 元件2.SCL, LCM1602_IIC3.SCL
  N9: 元件2.GPIO16, J1.pin2
  VSS: LCD2.VSS, LCM1602_IIC3.VSS
  VDD: LCD2.VDD, LCM1602_IIC3.VDD
  N10: LCD2.V0, LCM1602_IIC3.V0
  N11: LCD2.RS, LCM1602_IIC3.RS
  N12: LCD2.R/W, LCM1602_IIC3.RW
  N13: LCD2.E, LCM1602_IIC3.E
  N14: LCD2.DB0, LCM1602_IIC3.D0
  N15: LCD2.DB1, LCM1602_IIC3.D1
  N16: LCD2.DB2, LCM1602_IIC3.D2
  N17: LCD2.DB3, LCM1602_IIC3.D3
  N18: LCD2.DB4, LCM1602_IIC3.D4
  N19: LCD2.DB5, LCM1602_IIC3.D5
  N20: LCD2.DB6, LCM1602_IIC3.D6
  N21: LCD2.DB7, LCM1602_IIC3.D7
  N22: LCD2.LED+, LCM1602_IIC3.A
  N23: LCD2.LED-, LCM1602_IIC3.K
  N24: LCM1602_IIC3.GND, J1.pin1

notes:
  IRQ,RST,NSS,MOSI,MISO,SCK,GND,3.3V

custom parts:
  RFID-RC522-v2: A simple China made RFID-RC522 Reader; do check the pin labels, as this is a MFRC522 based clone.
  Adafruit T-Cobbler Plus: The Raspberry Pi has landed on the Maker World like a 40-GPIO pinned, quad-USB ported, credit card sized bomb of DIY joy. And while you can use most of our great Model B accessories by hooking up our downgrade cable, its probably a good time to upgrade your set up and accessorize using all of the 40 pins. That's why we now carry the Assembled Adafruit Pi T-Cobbler Plus - Breakout + Cable for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
  LCM1602 IIC: I2C-Module to use a 1602 or 2004 LCD on with the wire.h libory Serial LCD Modul
