# Fritzing sketch mcp3008可變電阻 (saved by Fritzing 0.9.3b)
breadboards: 1

parts:
  元件2 = Adafruit T-Cobbler Plus [part_number="Adafruit #1989 and #2028"]
  IC2 = MCP3008 8-channel 10-bit ADC [part_number=MCP3008]  # not connected
  R1 = Rotary Potentiometer (Small) [maximum_resistance=100kΩ package=THT]
  LED1 = LED - 5mm [color="Red (633nm)" package="5 mm [THT]"]
  R2 = Resistor [tolerance=±5% resistance=220 package=THT]

nets:
  N1: 元件2.+3.3V, R1.leg1
  N2: 元件2.GND, R1.leg2, LED1.cathode
  N3: 元件2.GPIO18, R2.Pin_0
  N4: LED1.anode, R2.Pin_1

custom parts:
  Adafruit T-Cobbler Plus: The Raspberry Pi has landed on the Maker World like a 40-GPIO pinned, quad-USB ported, credit card sized bomb of DIY joy. And while you can use most of our great Model B accessories by hooking up our downgrade cable, its probably a good time to upgrade your set up and accessorize using all of the 40 pins. That's why we now carry the Assembled Adafruit Pi T-Cobbler Plus - Breakout + Cable for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
